// Logisim project CIRCUITOS_VOGAIS.circ as structural Verilog: 2 circuits, main circuit main
module main (
  input  in_1,
  input  in_2,
  input  in_3
);

  wire bcd_7_1_a_2, bcd_7_1_b_2, bcd_7_1_c_2, bcd_7_1_d, bcd_7_1_e, bcd_7_1_f, bcd_7_1_g, bcd_7_2_a_2,
       bcd_7_2_b_2, bcd_7_2_c_2, bcd_7_2_d, bcd_7_2_e, bcd_7_2_f, bcd_7_2_g, clock_1_out;
  wire [2:0] counter_1_q;

  BCD_7 bcd_7_1 (
    .a_2(bcd_7_1_a_2), .b_2(bcd_7_1_b_2), .c_2(bcd_7_1_c_2), .d(bcd_7_1_d), .e(bcd_7_1_e), .f(bcd_7_1_f),
    .g(bcd_7_1_g), .A(in_1), .B(in_2), .C(in_3));
  Clock clock_1 (.out(clock_1_out));
  _7_Segment_Display u_7_segment_display_1 (
    .g(bcd_7_1_g), .f(bcd_7_1_f), .a(bcd_7_1_a_2), .b(bcd_7_1_b_2), .e(bcd_7_1_e), .d(bcd_7_1_d),
    .c(bcd_7_1_c_2));  // open: dp
  Counter #(.width(3), .max('h7)) counter_1 (.Q(counter_1_q), .clk(clock_1_out));  // open: load, D, count, carry, clr
  BCD_7 bcd_7_2 (
    .a_2(bcd_7_2_a_2), .b_2(bcd_7_2_b_2), .c_2(bcd_7_2_c_2), .d(bcd_7_2_d), .e(bcd_7_2_e), .f(bcd_7_2_f),
    .g(bcd_7_2_g), .A(counter_1_q[2]), .B(counter_1_q[1]), .C(counter_1_q[0]));
  _7_Segment_Display u_7_segment_display_2 (
    .g(bcd_7_2_g), .f(bcd_7_2_f), .a(bcd_7_2_a_2), .b(bcd_7_2_b_2), .e(bcd_7_2_e), .d(bcd_7_2_d),
    .c(bcd_7_2_c_2));  // open: dp
endmodule

module BCD_7 (
  input  A,
  input  B,
  input  C,
  output a_2,
  output b_2,
  output c_2,
  output d,
  output e,
  output f,
  output g
);

  and and_1 (g, ~A, ~B);  // AND_Gate
  or or_1 (b_2, B, ~C);  // OR_Gate
  or or_2 (d, A, C);
  or or_3 (e, C, ~B);  // OR_Gate
  or or_4 (a_2, g, C);

  assign c_2 = b_2;
  assign f = e;
endmodule
